# Fritzing sketch Lab5_currentMeasure (saved by Fritzing 0.9.3b)
breadboards: 1

parts:
  R1 = Resistor [tolerance=±5% resistance=100 package="0402 [SMD]"]
  Part2 = Adafruit Quad AlphaNumeric Featherwing - Pure Green [part_number="Adafruit #3129"]  # not connected
  Part3 = Adafruit Quad AlphaNumeric Featherwing - Blue [part_number="Adafruit #3128"]
  BAT1 = Battery Holders [package=battery-aaa]

nets:
  N1: R1.Pin_0, BAT1.-
  N2: R1.Pin_1, Part3.VBAT
  N3: Part3.A, BAT1.+

custom parts:
  Adafruit Quad AlphaNumeric Featherwing - Pure Green: This is the Green Adafruit 0.54" Dual Alphanumeric Display w/ FeatherWing Combo Pack! We also have these combo packs in Red, White, Yellow-Green, Blue, and Yellow. This is a nice, bright alphanumeric display that shows letters and numbers in a beautiful hue. It's super bright and designed for viewing from distances up to 23 feet (7 meters) away. Each of the digit sets have 14 segments on a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
  Adafruit Quad AlphaNumeric Featherwing - Blue: This is the Blue Adafruit 0.54" Dual Alphanumeric Display w/ FeatherWing Combo Pack! We also have these combo packs in Green, White, Yellow-Green, Red, and Yellow. This is a nice, bright alphanumeric display that shows letters and numbers in a beautiful hue. It's super bright and designed for viewing from distances up to 23 feet (7 meters) away. Each of the digit sets have 14 segments on a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
